# Fritzing sketch WithOptoCoupler (saved by Fritzing 0.8.5b)
circuit board: 8.46667cm x 5.64444cm
breadboards: 1

parts:
  IC1 = L293D [package=THT]
  U1 = Optocoupler [package=THT]
  U2 = Optocoupler [package=THT]
  U3 = Optocoupler [package=THT]
  U4 = Optocoupler [package=THT]
  VCC1 = Battery
  Part1 = Arduino Uno (Rev3)
  R1 = Resistor [tolerance=±5% resistance=220 package=THT]
  R2 = Resistor [tolerance=±5% resistance=220 package=THT]
  R3 = Resistor [tolerance=±5% resistance=220 package=THT]
  R4 = Resistor [tolerance=±5% resistance=220 package=THT]
  M1 = DC Motor
  M2 = DC Motor
  R5 = Resistor [tolerance=±5% resistance=10k package=THT]
  R6 = Resistor [tolerance=±5% resistance=10k package=THT]
  R7 = Resistor [tolerance=±5% resistance=10k package=THT]
  R8 = Resistor [tolerance=±5% resistance=10k package=THT]
  R9 = Resistor [tolerance=±5% resistance=220 package=THT]
  R10 = Resistor [tolerance=±5% resistance=220 package=THT]
  Q2 = NPN-Transistor [package="TO92 [THT]"]
  R11 = Resistor [tolerance=±5% resistance=220 package=THT]
  R12 = Resistor [tolerance=±5% resistance=220 package=THT]
  Q1 = NPN-Transistor [package="TO92 [THT]"]

nets:
  N1: IC1.Enable_1, IC1.+Vmotor, IC1.Enable_2, IC1.+V, U1.Pin_4, U1.Pin_5, U2.Pin_4, U2.Pin_5, U2.Pin_6, U3.Pin_5, U4.Pin_5, VCC1.+, R5.Pin_0, R6.Pin_0, R10.Pin_1, R12.Pin_1
  N2: IC1.In_1, Q2.C, R12.Pin_0
  N3: IC1.Out_1_(_Controlled_by_Enable_1_), M2.pin_1
  N4: IC1.0V, VCC1.-, R5.Pin_1, R6.Pin_1, R7.Pin_1, R8.Pin_1, Q2.E, Q1.E
  N5: IC1.Out_2_(_Controlled_by_Enable_1_), M2.pin_2
  N6: IC1.In_2, U3.Pin_4, R7.Pin_0, R11.Pin_1
  N7: IC1.In_3, U4.Pin_4, R8.Pin_0, R9.Pin_0
  N8: IC1.Out_3_(_Controlled_by_Enable_2_), M1.pin_2
  N9: IC1.Out_4_(_Controlled_by_Enable_2_), M1.pin_1
  N10: IC1.In_4, R10.Pin_0, Q1.C
  N11: U1.Pin_1, R1.Pin_1
  N12: U1.Pin_2, U2.Pin_1, U2.Pin_2, U2.Pin_3, U3.Pin_2, U4.Pin_2, Part1.GND, Part1.D5_PWM, R3.Pin_0, R3.Pin_1
  N13: U3.Pin_1, R4.Pin_1
  N14: U4.Pin_1, R2.Pin_1
  N15: Part1.D2, R2.Pin_0
  N16: Part1.D3_PWM, R1.Pin_0
  N17: Part1.D4, R4.Pin_0
  N18: R9.Pin_1, Q1.B
  N19: Q2.B, R11.Pin_0
